# Fritzing sketch Turnstile (saved by Fritzing 0.9.5d)
breadboards: 1

parts:
  Raspberry_Pi_1 = Raspberry Pi 3 [part_number=RPI-3-V1.2]
  IC1 = Rasberry Pi NIOR Camera [chip_label=IC package="DIP (Dual Inline) [THT]"]  # not connected
  元件1 = RFID-RC522-v2
  LED1 = RGB LED - (4 legs) [package="5 mm [THT]"]

nets:
  3V3: Raspberry_Pi_1.3v3, 元件1.3.3V
  N1: Raspberry_Pi_1.GIPO10, 元件1.MISO
  N2: Raspberry_Pi_1.GIPO9, 元件1.IRQ
  N3: Raspberry_Pi_1.GIPO11, 元件1.MOSI
  N4: Raspberry_Pi_1.GIPO21, LED1.red_cathode
  N5: Raspberry_Pi_1.GIPO20, LED1.green_cathode
  N6: Raspberry_Pi_1.GIPO16, LED1.blue_cathode
  N7: Raspberry_Pi_1.GIPO8, 元件1.SCK
  N8: Raspberry_Pi_1.GIPO25, 元件1.RST
  GND: Raspberry_Pi_1.GND, 元件1.GND, LED1.common_anode

custom parts:
  Rasberry Pi NIOR Camera: Camera
  RFID-RC522-v2: A simple China made RFID-RC522 Reader; do check the pin labels, as this is a MFRC522 based clone.
